// Logisim project q8-17.circ as structural Verilog: 1 circuit, main circuit main
module main (
  input  in_1
);

  wire and_1_out, and_2_out, and_3_out, clock_1_out, not_1_out, or_1_out, or_2_out, t_ff_1_q, t_ff_2_q,
       t_ff_2_qn, t_ff_3_q, t_ff_4_q, t_ff_4_qn;

  Clock clock_1 (.out(clock_1_out));
  T_Flip_Flop t_ff_1 (.T(or_2_out), .clk(clock_1_out), .Q(t_ff_1_q), .reset(not_1_out));  // open: Qn, preset
  not not_1 (not_1_out, in_1);
  or or_1 (or_1_out, and_1_out, t_ff_1_q);
  and and_1 (and_1_out, t_ff_2_q, t_ff_4_q);
  T_Flip_Flop t_ff_2 (
    .T(or_1_out), .clk(clock_1_out), .Q(t_ff_2_q), .Qn(t_ff_2_qn), .reset(not_1_out));  // open: preset
  or or_2 (or_2_out, t_ff_2_qn, t_ff_4_qn);
  and and_2 (and_2_out, t_ff_1_q, t_ff_2_q);
  T_Flip_Flop t_ff_3 (.T(and_2_out), .clk(clock_1_out), .Q(t_ff_3_q), .reset(not_1_out));  // open: Qn, preset
  and and_3 (and_3_out, and_2_out, t_ff_3_q);
  T_Flip_Flop t_ff_4 (
    .T(and_3_out), .clk(clock_1_out), .Q(t_ff_4_q), .Qn(t_ff_4_qn), .reset(not_1_out));  // open: preset
endmodule
