// Logisim project Tacsim2V5.circ as structural Verilog: 12 circuits, main circuit main
module CLA6 (
  input  Cin,
  input  [5:0] A,
  input  [5:0] B,
  output [5:0] Output,
  output Cout,
  output Overflow
);

  wire F7, F8, L1, L2, L3, L4, L5, L6, L7, L8, L9, L10, S1, S2, S3, S4, S5, S6, S7, S8, S9, S10, S11, S12,
       V1, V2, V3, V4, V5, V6, V7;

  xor xor_1 (L1, A[0], B[0]);
  and and_1 (L2, A[0], B[0]);
  xor xor_2 (L3, A[1], B[1]);
  and and_2 (L4, A[1], B[1]);
  xor xor_3 (L5, A[2], B[2]);
  and and_3 (L6, A[2], B[2]);
  xor xor_4 (L7, A[3], B[3]);
  and and_4 (L8, A[3], B[3]);
  and and_5 (L9, A[4], B[4]);
  and and_6 (L10, A[5], B[5]);
  and and_7 (S1, Cin, L1);
  and and_8 (S2, L3, L1, Cin);
  and and_9 (S3, L2, L3);
  and and_10 (S4, L1, L3, L5, Cin);
  and and_11 (S5, L2, L3, L5);
  and and_12 (S6, L4, L5);
  and and_13 (S7, L1, L3, L5, L7);
  and and_14 (S8, L2, L3, L5, L7);
  and and_15 (S9, L3, L3, L5, L7);
  and and_16 (S10, L4, L3, L5, L7);
  and and_17 (S11, L4, L5, L9);
  and and_18 (S12, L8, L9);
  or or_1 (V1, S1, L2);
  or or_2 (V2, S2, S3, L4);
  or or_3 (V3, S4, S5, S6, L6);
  or or_4 (V4, S7, S8, L6);
  or or_5 (V5, S9, S10, S11, L8);
  and and_19 (V6, Cin, S9);
  or or_6 (V7, S10, S11, S12, L10);
  xor xor_5 (Output[0], L1, Cin);
  xor xor_6 (Output[1], V1, L3);
  xor xor_7 (Output[2], V2, L5);
  xor xor_8 (Output[3], V3, L7);
  xor xor_9 (Output[4], V4, L9);
  xor xor_10 (Output[5], V5, L10);
  xor xor_11 (F7, Cout, Cin);
  xnor xnor_1 (F8, A[5], B[5]);
  or or_7 (Cout, V4, V5);
  and and_20 (Overflow, F7, F8);

  // Other names for the same wires on the sheet: a1 = A[0]; a2 = A[1]; a3 = A[2]; a4 = A[3]; a5 = A[4]; a6 = A[5];
  //   b1 = B[0]; b2 = B[1]; b3 = B[2]; b4 = B[3]; b5 = B[4]; b6 = B[5]; F1 = Output[0]; F2 = Output[1];
  //   F3 = Output[2]; F4 = Output[3]; F5 = Output[4]; F6 = Output[5]

  // Notes on the sheet:
  //   L-COLUMN
  //   S-COLUMN
  //   V-COLUMN
  //   F-COLUMN
  //   OUTPUT
endmodule

module ADD12 (
  input  Cin,
  input  [11:0] A,
  input  [11:0] B,
  input  Cin_2,
  input  [11:0] A_2,
  input  [11:0] B_2,
  output [11:0] Output,
  output Cout,
  output Overflow,
  output [11:0] Output_2,
  output Cout_2,
  output Overflow_2
);

  wire cla6_1_cout, n6bitadder_1_cout;

  _6BitAdder u_6bitadder_1 (
    .Cin(Cin), .A(A[5:0]), .B(B[5:0]), .Output(Output[5:0]), .Cout(n6bitadder_1_cout));  // open: Overflow
  _6BitAdder u_6bitadder_2 (
    .Cin(n6bitadder_1_cout), .A(A[11:6]), .B(B[11:6]), .Output(Output[11:6]), .Cout(Cout), .Overflow(Overflow));
  CLA6 cla6_1 (.Cin(Cin_2), .A(A_2[5:0]), .B(B_2[5:0]), .Output(Output_2[5:0]), .Cout(cla6_1_cout));  // open: Overflow
  CLA6 cla6_2 (
    .Cin(cla6_1_cout), .A(A_2[11:6]), .B(B_2[11:6]), .Output(Output_2[11:6]), .Cout(Cout_2),
    .Overflow(Overflow_2));
endmodule

module ADDSUB12 (
  input  [11:0] A,
  input  [11:0] B,
  input  Enable,
  input  Subtraction,
  input  Cin,
  output [11:0] Test,
  output [11:0] Sum,
  output Cout,
  output Overflow
);

  wire [11:0] inverter_1_output;

  Inverter inverter_1 (.Input(B), .Enable(Subtraction), .Output(inverter_1_output));
  ADD12 add12_1 (
    .Cin(Cin), .A(A), .B(inverter_1_output), .Output(Test), .Cout(Cout), .Overflow(Overflow));  // open: Cin_2, A_2, B_2, Output_2, Cout_2, Overflow_2
  Buffer buffer_1 (.Input(Test), .Enable(Enable), .Output(Sum));
endmodule

module Inverter (
  input  [11:0] Input,
  input  Enable,
  output [11:0] Output
);

  xor xor_1 (Output[0], Input[0], Enable);
  xor xor_2 (Output[1], Input[1], Enable);
  xor xor_3 (Output[2], Input[2], Enable);
  xor xor_4 (Output[3], Input[3], Enable);
  xor xor_5 (Output[4], Input[4], Enable);
  xor xor_6 (Output[5], Input[5], Enable);
  xor xor_7 (Output[6], Input[6], Enable);
  xor xor_8 (Output[7], Input[7], Enable);
  xor xor_9 (Output[8], Input[8], Enable);
  xor xor_10 (Output[9], Input[9], Enable);
  xor xor_11 (Output[10], Input[10], Enable);
  xor xor_12 (Output[11], Input[11], Enable);
endmodule

module Buffer (
  input  [11:0] Input,
  input  Enable,
  output [11:0] Output
);

  assign Output[0] = Enable ? Input[0] : 1'bz;  // Controlled_Buffer controlled_buffer_1
  assign Output[1] = Enable ? Input[1] : 1'bz;  // Controlled_Buffer controlled_buffer_2
  assign Output[2] = Enable ? Input[2] : 1'bz;  // Controlled_Buffer controlled_buffer_3
  assign Output[3] = Enable ? Input[3] : 1'bz;  // Controlled_Buffer controlled_buffer_4
  assign Output[4] = Enable ? Input[4] : 1'bz;  // Controlled_Buffer controlled_buffer_5
  assign Output[5] = Enable ? Input[5] : 1'bz;  // Controlled_Buffer controlled_buffer_6
  assign Output[6] = Enable ? Input[6] : 1'bz;  // Controlled_Buffer controlled_buffer_7
  assign Output[7] = Enable ? Input[7] : 1'bz;  // Controlled_Buffer controlled_buffer_8
  assign Output[8] = Enable ? Input[8] : 1'bz;  // Controlled_Buffer controlled_buffer_9
  assign Output[9] = Enable ? Input[9] : 1'bz;  // Controlled_Buffer controlled_buffer_10
  assign Output[10] = Enable ? Input[10] : 1'bz;  // Controlled_Buffer controlled_buffer_11
  assign Output[11] = Enable ? Input[11] : 1'bz;  // Controlled_Buffer controlled_buffer_12
endmodule

module RORC12x1 (
  input  [11:0] Input,
  input  Cin,
  output Cout,
  output [11:0] Output
);


  assign Cout = Input[0];
  assign Output = {Cin, Input[11:1]};
endmodule

module ROLC12X1 (
  input  Cin,
  input  [11:0] Input,
  output [11:0] Output,
  output Cout
);


  assign Cout = Input[11];
  assign Output = {Input[10:0], Cin};
endmodule

module ALU12 (
  input  [11:0] A,
  input  [11:0] B,
  input  Cin,
  input  [3:0] FUN,
  output [11:0] S,
  output Cout,
  output Overflow
);

  wire ADD_SUB_Cout, ADDSUB_Overflow, Enable_Subtraction, m, ROLC_Cin, ROLC_Cout, RORC_Cout;
  wire [2:0] MUX_Instruct;
  wire [11:0] ADD_Output, ADDSUB_Input_B, AND_Output, OR_Output, ROLC_Output, RORC_Output, XOR_Output;

  Multiplexer #(.enable("false"), .select(3), .width(12)) multiplexer_1 (
    .in0(B), .in1(B), .in2(12'h1), .in3(12'h1), .out(ADDSUB_Input_B), .sel(MUX_Instruct));  // open: in4, in5, in6, in7
  ALUMap alumap_1 (
    .o0(FUN[3]), .o1(FUN[2]), .o2(FUN[1]), .o3(FUN[0]), .s0(MUX_Instruct[2]), .s1(MUX_Instruct[1]),
    .s2(MUX_Instruct[0]), .m(m));  // open: s3
  Multiplexer #(.enable("false")) multiplexer_2 (.in0(Cin), .in1(1'b0), .out(ROLC_Cin), .sel(m));
  ADDSUB12 addsub12_1 (
    .A(A), .B(ADDSUB_Input_B), .Enable(1'b1), .Subtraction(Enable_Subtraction), .Cin(1'b0), .Sum(ADD_Output),
    .Cout(ADD_SUB_Cout), .Overflow(ADDSUB_Overflow));  // open: Test
  Multiplexer #(.enable("false"), .select(3)) multiplexer_3 (
    .in0(1'b0), .in1(1'b1), .in2(m), .in3(1'b0), .in4(1'b0), .in5(1'b0), .in6(1'b0), .in7(1'b0),
    .out(Enable_Subtraction), .sel(MUX_Instruct));
  assign AND_Output = A & B;  // AND_Gate and_1, 12 bits wide
  assign OR_Output = A | B;  // OR_Gate or_1, 12 bits wide
  assign XOR_Output = A ^ B;  // XOR_Gate xor_1, 12 bits wide
  RORC12x1 rorc12x1_1 (.Input(A), .Cin(Cin), .Cout(RORC_Cout), .Output(RORC_Output));
  ROLC12X1 rolc12x1_1 (.Cin(ROLC_Cin), .Input(A), .Output(ROLC_Output), .Cout(ROLC_Cout));
  Multiplexer #(.enable("false"), .select(3)) multiplexer_4 (
    .in0(ADD_SUB_Cout), .in1(ADD_SUB_Cout), .in2(ADD_SUB_Cout), .in3(1'b0), .in4(1'b0), .in5(1'b0),
    .in6(RORC_Cout), .in7(ROLC_Cout), .out(Cout), .sel(MUX_Instruct));
  Multiplexer #(.enable("false"), .select(3)) multiplexer_5 (
    .in0(ADDSUB_Overflow), .in1(ADDSUB_Overflow), .in2(ADDSUB_Overflow), .in3(1'b0), .in4(1'b0), .in5(1'b0),
    .in6(1'b0), .in7(1'b0), .out(Overflow), .sel(MUX_Instruct));
  Multiplexer #(.enable("false"), .select(3), .width(12)) multiplexer_6 (
    .in0(ADD_Output), .in1(ADD_Output), .in2(ADD_Output), .in3(AND_Output), .in4(OR_Output),
    .in5(XOR_Output), .in6(RORC_Output), .in7(ROLC_Output), .out(S), .sel(MUX_Instruct));

  // Other names for the same wires on the sheet: ALU_Cout = Cout; ALU_Output[11:0] = S; ALU_Overflow = Overflow;
  //   FUN_Input[3:0] = FUN; RO_SH_Left_Mux = m; Cin_Main = Cin; RORC_Cin = Cin; ADDSUB_Output[11:0] = ADD_Output;
  //   INC_DEC_Output[11:0] = ADD_Output; SUB_Output[11:0] = ADD_Output; A_Input[11:0] = A; ADDSUB_Input_A[11:0] = A;
  //   AND_Input_A[11:0] = A; OR_Input_A[11:0] = A; ROLC_Input[11:0] = A; RORC_Input[11:0] = A; XOR_Input_A[11:0] = A;
  //   AND_Input_B[11:0] = B; B_Input[11:0] = B; OR_Input_B[11:0] = B; XOR_Input_B[11:0] = B

  // Notes on the sheet:
  //   0000 --- ADD
  //   0001 --- SUB
  //   0010 --- INC
  //   0011 --- DEC
  //   0100 --- AND
  //   0101 --- OR
  //   0110 --- XOR
  //   0111 --- RORC
  //   1000 --- ROLC
  //   1001 --- ASL
  //   MAIN Inputs
  //   0000 --- ADD
  //   0001 --- SUB
  //   0010 --- INC
  //   1010 --- DEC
  //   0011 --- AND
  //   0100 --- OR
  //   0101 --- XOR
  //   0110 --- RORC
  //   0111 --- ROLC
  //   1111 --- ASL
  //   Input Control
  //   FUN Breakdown
  //   Functions
  //   Enable_Sub
  //   MUX Control
  //   Output Control
  //   MAIN Outputs
  //   Enable_Sub
  //   Cout Control
  //   Overflow Control
endmodule

module _1BitAdder (
  input  Cin,
  input  A,
  input  B,
  output Output,
  output Cout
);

  wire and_1_out, and_2_out, xor_1_out;

  xor xor_1 (xor_1_out, A, B);
  and and_1 (and_1_out, A, B);
  and and_2 (and_2_out, Cin, xor_1_out);
  xor xor_2 (Output, Cin, xor_1_out);
  or or_1 (Cout, and_2_out, and_1_out);
endmodule

module _6BitAdder (
  input  Cin,
  input  [5:0] A,
  input  [5:0] B,
  output [5:0] Output,
  output Cout,
  output Overflow
);

  wire F7, F8, n1bitadder_1_cout, n1bitadder_2_cout, n1bitadder_3_cout, n1bitadder_4_cout, n1bitadder_5_cout;

  _1BitAdder u_1bitadder_1 (.Cin(Cin), .A(A[0]), .B(B[0]), .Output(Output[0]), .Cout(n1bitadder_1_cout));
  _1BitAdder u_1bitadder_2 (.Cin(n1bitadder_1_cout), .A(A[1]), .B(B[1]), .Output(Output[1]), .Cout(n1bitadder_2_cout));
  _1BitAdder u_1bitadder_3 (.Cin(n1bitadder_2_cout), .A(A[2]), .B(B[2]), .Output(Output[2]), .Cout(n1bitadder_3_cout));
  _1BitAdder u_1bitadder_4 (.Cin(n1bitadder_3_cout), .A(A[3]), .B(B[3]), .Output(Output[3]), .Cout(n1bitadder_4_cout));
  _1BitAdder u_1bitadder_5 (.Cin(n1bitadder_4_cout), .A(A[4]), .B(B[4]), .Output(Output[4]), .Cout(n1bitadder_5_cout));
  _1BitAdder u_1bitadder_6 (.Cin(n1bitadder_5_cout), .A(A[5]), .B(B[5]), .Output(Output[5]), .Cout(Cout));
  xor xor_1 (F7, Cout, Cin);
  xnor xnor_1 (F8, A[5], B[5]);
  and and_1 (Overflow, F7, F8);

  // Other names for the same wires on the sheet: a6 = A[5]; b6 = B[5]
endmodule

module ALUDemo (
  output Cout,
  output Overflow
);

  wire dipswitch_2_sw8;
  wire [3:0] alu12_1_s_2, dipswitch_1_sw4, dipswitch_2_sw4, dipswitch_3_sw4;
  wire [7:0] alu12_1_s;
  wire [7:4] dipswitch_1_sw8;
  wire [11:0] dipswitch_4_sw8;

  Hex_Digit_Display hex_digit_display_1 (.value(dipswitch_1_sw4));  // open: dp
  DipSwitch dipswitch_1 (
    .sw1(dipswitch_1_sw4[3]), .sw2(dipswitch_1_sw4[2]), .sw3(dipswitch_1_sw4[1]), .sw4(dipswitch_1_sw4[0]),
    .sw5(dipswitch_1_sw8[7]), .sw6(dipswitch_1_sw8[6]), .sw7(dipswitch_1_sw8[5]), .sw8(dipswitch_1_sw8[4]));
  Hex_Digit_Display hex_digit_display_2 (.value(dipswitch_3_sw4));  // open: dp
  Hex_Digit_Display hex_digit_display_3 (.value(dipswitch_1_sw8));  // open: dp
  DipSwitch dipswitch_2 (
    .sw1(dipswitch_2_sw4[3]), .sw2(dipswitch_2_sw4[2]), .sw3(dipswitch_2_sw4[1]), .sw4(dipswitch_2_sw4[0]),
    .sw8(dipswitch_2_sw8));  // open: sw5, sw6, sw7
  DipSwitch dipswitch_3 (
    .sw1(dipswitch_3_sw4[3]), .sw2(dipswitch_3_sw4[2]), .sw3(dipswitch_3_sw4[1]), .sw4(dipswitch_3_sw4[0]),
    .sw5(dipswitch_4_sw8[11]), .sw6(dipswitch_4_sw8[10]), .sw7(dipswitch_4_sw8[9]), .sw8(dipswitch_4_sw8[8]));
  PLA #(.in_width(4), .\table ("0000 00 # +\n0001 00 # -\n0010 00 # +1\n0011 00 # -1\n0100 00 # AND\n0101 00 # OR\n0110 00 # XOR\n0111 00 # ROR\n1000 00 # ROL\n1001 00 # ASL")) pla_1 (.in(dipswitch_2_sw4));  // open: out
  Hex_Digit_Display hex_digit_display_4 (.value(dipswitch_4_sw8[11:8]));  // open: dp
  Hex_Digit_Display hex_digit_display_5 (.value(dipswitch_4_sw8[7:4]));  // open: dp
  DipSwitch dipswitch_4 (
    .sw1(dipswitch_4_sw8[7]), .sw2(dipswitch_4_sw8[6]), .sw3(dipswitch_4_sw8[5]), .sw4(dipswitch_4_sw8[4]),
    .sw5(dipswitch_4_sw8[3]), .sw6(dipswitch_4_sw8[2]), .sw7(dipswitch_4_sw8[1]), .sw8(dipswitch_4_sw8[0]));
  Hex_Digit_Display hex_digit_display_6 (.value(dipswitch_4_sw8[3:0]));  // open: dp
  Hex_Digit_Display hex_digit_display_7 (.value(alu12_1_s_2));  // open: dp
  ALU12 alu12_1 (
    .A({dipswitch_1_sw4, dipswitch_1_sw8, dipswitch_3_sw4}), .B(dipswitch_4_sw8), .Cin(dipswitch_2_sw8),
    .FUN(dipswitch_2_sw4), .S({alu12_1_s_2, alu12_1_s}), .Cout(Cout), .Overflow(Overflow));
  Hex_Digit_Display hex_digit_display_8 (.value(alu12_1_s[7:4]));  // open: dp
  Hex_Digit_Display hex_digit_display_9 (.value(alu12_1_s[3:0]));  // open: dp

  // Notes on the sheet:
  //   =
  //   0000 --- ADD
  //   0001 --- SUB
  //   0010 --- INC
  //   0011 --- DEC
  //   0100 --- AND
  //   0101 --- OR
  //   0110 --- XOR
  //   0111 --- RORC
  //   1000 --- ROLC
  //   1001 --- ASL
endmodule

module ALUMap (
  input  o0,
  input  o1,
  input  o2,
  input  o3,
  output s0,
  output s1,
  output s2,
  output s3,
  output m
);

  wire and_8_out, and_9_out, and_10_out, and_11_out, and_12_out, and_13_out, o0_o1_prime_o2, o0_prime,
       o0_prime_o1_prime_o2, o1_o2_o3_prime, o1_o2_prime_o3_prime, o1_prime, o1_prime_o2_prime_o3, o2_o3,
       o2_prime, o3_prime, or_3_out;

  not not_1 (o0_prime, o0);
  not not_2 (o1_prime, o1);
  not not_3 (o2_prime, o2);
  not not_4 (o3_prime, o3);
  and and_1 (o1_o2_prime_o3_prime, o1, o2_prime, o3_prime);
  and and_2 (o0_prime_o1_prime_o2, o2, o0_prime, o1_prime);
  and and_3 (o2_o3, o2, o3);
  and and_4 (o1_prime_o2_prime_o3, o1_prime, o2_prime, o3);
  and and_5 (o1_o2_o3_prime, o1, o2, o3_prime);
  and and_6 (o0_o1_prime_o2, o0, o1_prime, o2);
  or or_1 (s1, o1_o2_prime_o3_prime, o0_prime_o1_prime_o2, o2_o3, o0);
  or or_2 (s2, o1_prime_o2_prime_o3, o1_o2_prime_o3_prime, o1_o2_o3_prime, o0);
  and and_7 (s3, o0, o1_prime, o3);
  and and_8 (and_8_out, o0, o1_prime);
  or or_3 (or_3_out, and_8_out, o1);
  and and_9 (and_9_out, o0_prime, o1, o2_prime, o3);
  and and_10 (and_10_out, o0, o1_prime, o2_prime, o3_prime);
  and and_11 (and_11_out, o0, o1_prime, o2_prime, o3);
  and and_12 (and_12_out, o0_prime, o1, o2, o3);
  and and_13 (and_13_out, o0_prime, o1, o2, o3_prime);
  or or_4 (s0, and_9_out, and_12_out, and_10_out, and_13_out, and_11_out);

  assign m = o3;

  // Other names for the same wires on the sheet: o0_o1_prime = s0; s1_Combo = s1; s2_Combo = s2

  // Notes on the sheet:
  //   s1
  //   s2
  //   s3
  //   0000 --- ADD
  //   0001 --- SUB
  //   0010 --- INC
  //   0011 --- DEC
  //   0100 --- AND
  //   0101 --- OR
  //   0110 --- XOR
  //   0111 --- RORC
  //   1000 --- ROLC
  //   1001 --- ASL
  //   Output
  //   Ref Sheet
  //   0000 --- ADD
  //   0001 --- SUB
  //   0010 --- INC
  //   1010 --- DEC
  //   0011 --- AND
  //   0100 --- OR
  //   0101 --- XOR
  //   0110 --- RORC
  //   0111 --- ROLC
  //   1111 --- ASL
  //   s0
  //   o0’ o1 o2’ o3 + o0’ o1 o2 o3’ + 
  //   o0’ o1 o2 o3 + o0 o1’ o2’ o3’ + o0 o1’ o2’ o3
endmodule
